// Logisim project ALU.circ as structural Verilog: 20 circuits, main circuit ALU
module ALU (
  input  [7:0] A,
  input  [7:0] B,
  input  [3:0] slct,
  output [7:0] S,
  output Err
);

  wire alu_arithm_1_c_out, bloc_shift_1_err;
  wire [7:0] alu_arithm_1_s, alu_comp_1_s, alu_logic_1_s, bloc_shift_1_s;

  alu_arithm alu_arithm_1 (.A(A), .B(B), .slct(slct[0]), .S(alu_arithm_1_s), .C_out(alu_arithm_1_c_out));
  alu_logic alu_logic_1 (.A(A), .B(B), .slct(slct[1:0]), .S(alu_logic_1_s));
  alu_comp alu_comp_1 (.A(A), .B(B), .slct(slct[1:0]), .S(alu_comp_1_s));
  bloc_shift bloc_shift_1 (.slct(slct[1:0]), .A(A), .Err(bloc_shift_1_err), .S(bloc_shift_1_s));
  Multiplexer #(.select(2), .width(8)) multiplexer_1 (
    .in0(alu_arithm_1_s), .in1(alu_logic_1_s), .in2(alu_comp_1_s), .in3(bloc_shift_1_s), .out(S),
    .sel(slct[3:2]));
  Multiplexer #(.select(2)) multiplexer_2 (
    .in0(alu_arithm_1_c_out), .in3(bloc_shift_1_err), .out(Err), .sel(slct[3:2]));  // open: in1, in2
endmodule

module half_adder (
  input  A,
  input  B,
  output S,
  output C
);

  and and_1 (C, B, A);
  xor xor_1 (S, A, B);

  // Notes on the sheet:
  //   Sortie
  //   Retenue
endmodule

module full_adder (
  input  A,
  input  B,
  input  C_In,
  output S,
  output C_Out
);

  wire half_adder_1_c, half_adder_1_s, half_adder_2_c;

  half_adder half_adder_1 (.A(A), .B(B), .S(half_adder_1_s), .C(half_adder_1_c));
  half_adder half_adder_2 (.A(C_In), .B(half_adder_1_s), .S(S), .C(half_adder_2_c));
  or or_1 (C_Out, half_adder_2_c, half_adder_1_c);
endmodule

module bits_adder (
  input  [7:0] A,
  input  [7:0] B,
  input  C_init,
  output [7:0] S,
  output C_out
);

  wire full_adder_1_c_out, full_adder_2_c_out, full_adder_3_c_out, full_adder_4_c_out, full_adder_5_c_out,
       full_adder_6_c_out, full_adder_7_c_out;

  full_adder full_adder_1 (.A(A[0]), .B(B[0]), .C_In(C_init), .S(S[0]), .C_Out(full_adder_1_c_out));
  full_adder full_adder_2 (.A(A[1]), .B(B[1]), .C_In(full_adder_1_c_out), .S(S[1]), .C_Out(full_adder_2_c_out));
  full_adder full_adder_3 (.A(A[2]), .B(B[2]), .C_In(full_adder_2_c_out), .S(S[2]), .C_Out(full_adder_3_c_out));
  full_adder full_adder_4 (.A(A[3]), .B(B[3]), .C_In(full_adder_3_c_out), .S(S[3]), .C_Out(full_adder_4_c_out));
  full_adder full_adder_5 (.A(A[4]), .B(B[4]), .C_In(full_adder_4_c_out), .S(S[4]), .C_Out(full_adder_5_c_out));
  full_adder full_adder_6 (.A(A[5]), .B(B[5]), .C_In(full_adder_5_c_out), .S(S[5]), .C_Out(full_adder_6_c_out));
  full_adder full_adder_7 (.A(A[6]), .B(B[6]), .C_In(full_adder_6_c_out), .S(S[6]), .C_Out(full_adder_7_c_out));
  full_adder full_adder_8 (.A(A[7]), .B(B[7]), .C_In(full_adder_7_c_out), .S(S[7]), .C_Out(C_out));
endmodule

module bits_supr (
  input  [7:0] A,
  input  [7:0] B,
  output [7:0] S,
  output C_out
);

  wire [7:0] not_1_out;

  assign not_1_out = ~B;  // NOT_Gate not_1, 8 bits wide
  bits_adder bits_adder_1 (.A(not_1_out), .B(A), .C_init(1'b1), .S(S), .C_out(C_out));

  // Notes on the sheet:
  //   C_out = 1 si A>=B C_out=0 SI A<B
endmodule

module alu_arithm (
  input  [7:0] A,
  input  [7:0] B,
  input  slct,
  output [7:0] S,
  output C_out
);

  wire bits_adder_1_c_out;
  wire [7:0] bits_adder_1_s, bits_supr_1_s;

  bits_adder bits_adder_1 (.A(A), .B(B), .C_init(1'b0), .S(bits_adder_1_s), .C_out(bits_adder_1_c_out));
  bits_supr bits_supr_1 (.A(A), .B(B), .S(bits_supr_1_s));  // open: C_out
  Multiplexer #(.width(8)) multiplexer_1 (.in0(bits_adder_1_s), .in1(bits_supr_1_s), .out(S), .sel(slct));
  Multiplexer multiplexer_2 (.in0(bits_adder_1_c_out), .out(C_out), .sel(slct));  // open: in1
endmodule

module bits_and (
  input  [7:0] A,
  input  [7:0] B,
  output [7:0] S
);

  and and_1 (S[0], B[0], A[0]);
  and and_2 (S[1], B[1], A[1]);
  and and_3 (S[2], B[2], A[2]);
  and and_4 (S[3], B[3], A[3]);
  and and_5 (S[4], B[4], A[4]);
  and and_6 (S[5], B[5], A[5]);
  and and_7 (S[6], B[6], A[6]);
  // AND_Gate and_8 has open pins: in0=B[7], in1=A[7], out=open
endmodule

module bits_or (
  input  [7:0] A,
  input  [7:0] B,
  output [7:0] S
);

  or or_1 (S[0], B[0], A[0]);
  or or_2 (S[1], B[1], A[1]);
  or or_3 (S[2], B[2], A[2]);
  or or_4 (S[3], B[3], A[3]);
  or or_5 (S[4], B[4], A[4]);
  or or_6 (S[5], B[5], A[5]);
  or or_7 (S[6], B[6], A[6]);
  or or_8 (S[7], B[7], A[7]);
endmodule

module bits_xor (
  input  [7:0] A,
  input  [7:0] B,
  output [7:0] S
);

  xor xor_1 (S[0], B[0], A[0]);
  xor xor_2 (S[1], B[1], A[1]);
  xor xor_3 (S[2], B[2], A[2]);
  xor xor_4 (S[3], B[3], A[3]);
  xor xor_5 (S[4], B[4], A[4]);
  xor xor_6 (S[5], B[5], A[5]);
  xor xor_7 (S[6], B[6], A[6]);
  xor xor_8 (S[7], B[7], A[7]);
endmodule

module alu_logic (
  input  [7:0] A,
  input  [7:0] B,
  input  [1:0] slct,
  output [7:0] S
);

  wire [7:0] bits_and_1_s, bits_or_1_s, bits_xor_1_s;

  bits_and bits_and_1 (.A(A), .B(B), .S(bits_and_1_s));
  bits_or bits_or_1 (.A(A), .B(B), .S(bits_or_1_s));
  bits_xor bits_xor_1 (.A(A), .B(B), .S(bits_xor_1_s));
  Multiplexer #(.select(2), .width(8)) multiplexer_1 (
    .in0(bits_and_1_s), .in1(bits_or_1_s), .in2(bits_xor_1_s), .out(S), .sel(slct));  // open: in3
endmodule

module bits_equals (
  input  [7:0] A,
  input  [7:0] B,
  output S
);

  wire xnor_1_out, xnor_2_out, xnor_3_out, xnor_4_out, xnor_5_out, xnor_6_out, xnor_7_out, xnor_8_out;

  xnor xnor_1 (xnor_1_out, B[0], A[0]);
  xnor xnor_2 (xnor_2_out, B[1], A[1]);
  xnor xnor_3 (xnor_3_out, B[2], A[2]);
  xnor xnor_4 (xnor_4_out, B[3], A[3]);
  xnor xnor_5 (xnor_5_out, B[4], A[4]);
  xnor xnor_6 (xnor_6_out, B[5], A[5]);
  xnor xnor_7 (xnor_7_out, B[6], A[6]);
  xnor xnor_8 (xnor_8_out, B[7], A[7]);
  and and_1 (S, xnor_1_out, xnor_2_out, xnor_3_out, xnor_4_out, xnor_5_out, xnor_6_out, xnor_7_out, xnor_8_out);
endmodule

module bits_diff (
  input  [7:0] A,
  input  [7:0] B,
  output S
);

  wire bits_equals_1_s;

  bits_equals bits_equals_1 (.A(A), .B(B), .S(bits_equals_1_s));
  not not_1 (S, bits_equals_1_s);
endmodule

module bits_inf (
  input  [7:0] A,
  input  [7:0] B,
  output S
);

  wire bits_supr_1_c_out;

  bits_supr bits_supr_1 (.A(A), .B(B), .C_out(bits_supr_1_c_out));  // open: S
  not not_1 (S, bits_supr_1_c_out);
endmodule

module bits_sup (
  input  [7:0] A,
  input  [7:0] B,
  output S
);

  wire bits_supr_1_c_out, or_1_out;
  wire [7:0] bits_supr_1_s;

  bits_supr bits_supr_1 (.A(A), .B(B), .S(bits_supr_1_s), .C_out(bits_supr_1_c_out));
  or or_1 (or_1_out, bits_supr_1_s[0], bits_supr_1_s[1], bits_supr_1_s[2], bits_supr_1_s[3], bits_supr_1_s[4], bits_supr_1_s[5], bits_supr_1_s[6], bits_supr_1_s[7]);
  and and_1 (S, or_1_out, bits_supr_1_c_out);
endmodule

module alu_comp (
  input  [7:0] A,
  input  [7:0] B,
  input  [1:0] slct,
  output [7:0] S
);

  wire bits_diff_1_s, bits_equals_1_s, bits_inf_1_s, bits_sup_1_s, multiplexer_1_out;

  bits_equals bits_equals_1 (.A(A), .B(B), .S(bits_equals_1_s));
  bits_diff bits_diff_1 (.A(A), .B(B), .S(bits_diff_1_s));
  bits_inf bits_inf_1 (.A(A), .B(B), .S(bits_inf_1_s));
  bits_sup bits_sup_1 (.A(A), .B(B), .S(bits_sup_1_s));
  Multiplexer #(.select(2)) multiplexer_1 (
    .in0(bits_equals_1_s), .in1(bits_diff_1_s), .in2(bits_inf_1_s), .in3(bits_sup_1_s),
    .out(multiplexer_1_out), .sel(slct));
  assign S = {{7{1'b0}}, multiplexer_1_out};  // Bit_Extender bit_extender_1
endmodule

module lsl (
  input  [7:0] A,
  output Err,
  output [7:0] S
);


  assign Err = A[7];
  assign S = {A[6:0], 1'b0};
endmodule

module lsr (
  input  [7:0] A,
  output Err,
  output [7:0] S
);


  assign Err = A[0];
  assign S = {1'b0, A[7:1]};
endmodule

module rotar (
  input  [7:0] A,
  output [7:0] S
);


  assign S = {A[0], A[7:1]};
endmodule

module rotal (
  input  [7:0] A,
  output [7:0] S
);


  assign S = {A[6:0], A[7]};
endmodule

module bloc_shift (
  input  [1:0] slct,
  input  [7:0] A,
  output Err,
  output [7:0] S
);

  wire lsl_1_err, lsr_1_err;
  wire [7:0] lsl_1_s, lsr_1_s, rotal_1_s, rotar_1_s;

  lsl lsl_1 (.A(A), .Err(lsl_1_err), .S(lsl_1_s));
  lsr lsr_1 (.A(A), .Err(lsr_1_err), .S(lsr_1_s));
  rotar rotar_1 (.A(A), .S(rotar_1_s));
  rotal rotal_1 (.A(A), .S(rotal_1_s));
  Multiplexer #(.select(2)) multiplexer_1 (.in0(lsl_1_err), .in1(lsr_1_err), .out(Err), .sel(slct));  // open: in2, in3
  Multiplexer #(.select(2), .width(8)) multiplexer_2 (
    .in0(lsl_1_s), .in1(lsr_1_s), .in2(rotar_1_s), .in3(rotal_1_s), .out(S), .sel(slct));
endmodule
