// Logisim project alu_registry.circ as structural Verilog: 1 circuit, main circuit alu_registry
module alu_registry (
  input  [3:0] slctB,
  input  [3:0] slctA,
  input  [7:0] C,
  input  [3:0] slctOP,
  input  [3:0] slctC,
  output [7:0] sA,
  output [7:0] S,
  output out_8,
  output S7_1bit
);

  wire decoder_1_out1, decoder_1_out2, decoder_1_out3, decoder_1_out4, decoder_1_out5, decoder_1_out6,
       decoder_1_out7, decoder_1_out8;
  wire [7:0] bit_extender_1_out, multiplexer_2_out, registry_1_s0, registry_1_s1, registry_1_s2,
       registry_1_s3, registry_1_s4, registry_1_s5, registry_1_s6, registry_1_s7_8bit;

  Decoder #(.select(4)) decoder_1 (
    .out1(decoder_1_out1), .out2(decoder_1_out2), .out3(decoder_1_out3), .out4(decoder_1_out4),
    .out5(decoder_1_out5), .out6(decoder_1_out6), .out7(decoder_1_out7), .out8(decoder_1_out8), .sel(slctC),
    .en(1'b1));  // open: out0, out9, out10, out11, out12, out13, out14, out15
  registry registry_1 (
    .C(C), .R0(decoder_1_out1), .R1(decoder_1_out2), .R2(decoder_1_out3), .R3(decoder_1_out4),
    .R4(decoder_1_out5), .R5(decoder_1_out6), .R6(decoder_1_out7), .R7(decoder_1_out8), .S0(registry_1_s0),
    .S1(registry_1_s1), .S2(registry_1_s2), .S3(registry_1_s3), .S4(registry_1_s4), .S5(registry_1_s5),
    .S6(registry_1_s6), .S7_8bit(registry_1_s7_8bit), .S7_1bit(S7_1bit));
  assign bit_extender_1_out = {{7{1'b0}}, S7_1bit};  // Bit_Extender bit_extender_1
  Multiplexer #(.select(4), .width(8)) multiplexer_1 (
    .in0({8{1'b0}}), .in1(registry_1_s0), .in2(registry_1_s1), .in3(registry_1_s2), .in4(registry_1_s3),
    .in5(registry_1_s4), .in6(registry_1_s5), .in7(registry_1_s6), .in8(registry_1_s7_8bit),
    .in9(bit_extender_1_out), .out(sA), .sel(slctA));  // open: in10, in11, in12, in13, in14, in15
  Multiplexer #(.select(4), .width(8)) multiplexer_2 (
    .in0({8{1'b0}}), .in1(registry_1_s0), .in2(registry_1_s1), .in3(registry_1_s2), .in4(registry_1_s3),
    .in5(registry_1_s4), .in6(registry_1_s5), .in7(registry_1_s6), .in8(registry_1_s7_8bit),
    .in9(bit_extender_1_out), .out(multiplexer_2_out), .sel(slctB));  // open: in10, in11, in12, in13, in14, in15
  ALU alu_1 (.A(sA), .B(multiplexer_2_out), .slct(slctOP), .S(S), .Err(out_8));
endmodule
