// Logisim project cpu_pc.circ as structural Verilog: 1 circuit, main circuit pc
module pc (
  input  [7:0] RAM,
  input  [7:0] ALU,
  input  jmp,
  input  [7:0] addr8,
  input  [1:0] slctREG_IN,
  output [7:0] addr_data,
  output [7:0] REG_IN,
  output [7:0] addr_code
);

  wire [7:0] adder_1_out, bits_registry_1_s;

  Multiplexer #(.width(8)) multiplexer_1 (.in0(adder_1_out), .in1(addr8), .out(addr_code), .sel(jmp));
  bits_registry bits_registry_1 (.A(addr_code), .We(1'b1), .S(bits_registry_1_s));
  Adder adder_1 (.a(bits_registry_1_s), .b(8'h1), .out(adder_1_out));  // open: cin, cout
  Multiplexer #(.select(2), .width(8)) multiplexer_2 (
    .in0(ALU), .in1(RAM), .in2(addr8), .out(REG_IN), .sel(slctREG_IN));  // open: in3

  assign addr_data = addr8;
endmodule
