// Logisim project decode.circ as structural Verilog: 5 circuits, main circuit decode
module fetch_decode (
  input  [23:0] F_24bits,
  input  zero,
  output jump,
  output [7:0] ADDR8,
  output [1:0] slctREG_in,
  output [3:0] slctRegWrite,
  output [3:0] slctRegB,
  output [3:0] slctRegA,
  output [3:0] slctOp,
  output stor
);

  wire [23:0] fetch_1_d_24bits, multiplexer_1_out;

  fetch fetch_1 (.F_24bits(F_24bits), .D_24bits(fetch_1_d_24bits));
  Multiplexer #(.width(24)) multiplexer_1 (
    .in0(fetch_1_d_24bits), .in1({24{1'b0}}), .out(multiplexer_1_out));  // open: sel
  decode decode_1 (
    .instru(multiplexer_1_out), .zero(zero), .slctOp(slctOp), .slctREG_in(slctREG_in), .jump(jump),
    .slctRegA(slctRegA), .stor(stor), .ADDR8(ADDR8), .slctRegB(slctRegB), .slctRegWrite(slctRegWrite));
endmodule

module decode (
  input  [23:0] instru,
  input  zero,
  output [3:0] slctOp,
  output [1:0] slctREG_in,
  output jump,
  output [3:0] slctRegA,
  output stor,
  output [7:0] ADDR8,
  output [3:0] slctRegB,
  output [3:0] slctRegWrite
);

  wire [23:0] registry_24bits_1_s;

  registry_24bits registry_24bits_1 (.instru(instru), .We(1'b1), .S(registry_24bits_1_s));
  decode_instru decode_instru_1 (
    .instru(registry_24bits_1_s), .zero(zero), .slctOp(slctOp), .slctREG_in(slctREG_in), .jump(jump),
    .slctRegA(slctRegA), .stor(stor), .ADRR8(ADDR8), .slctRegB(slctRegB), .slctRegWrite(slctRegWrite));
endmodule

module fetch (
  input  [23:0] F_24bits,
  output [23:0] D_24bits
);

  registry_24bits registry_24bits_1 (.instru(F_24bits), .We(1'b1), .S(D_24bits));
endmodule

module decode_instru (
  input  [23:0] instru,
  input  zero,
  output [3:0] slctOp,
  output [1:0] slctREG_in,
  output jump,
  output [3:0] slctRegA,
  output stor,
  output [7:0] ADRR8,
  output [3:0] slctRegB,
  output [3:0] slctRegWrite
);

  wire and_1_out, and_2_out, and_3_out, not_2_out, or_2_out, or_3_out, type_op_decode_1_jeq,
       type_op_decode_1_jne, type_op_decode_1_jump;
  wire [3:0] multiplexer_1_out;
  wire [23:0] not_1_out, or_1_out;

  type_op_decode type_op_decode_1 (
    .type_op(instru[23:20]), .op(instru[19:16]), .slcOp(slctOp), .slctREG_in(slctREG_in),
    .jump(type_op_decode_1_jump), .stor(stor), .jne(type_op_decode_1_jne), .jeq(type_op_decode_1_jeq));
  Multiplexer #(.select(4), .width(4)) multiplexer_1 (
    .in0(instru[3:0]), .in1(instru[3:0]), .in2(instru[3:0]), .in3(instru[3:0]), .in4(instru[3:0]),
    .in5(instru[3:0]), .in6(instru[3:0]), .in7(instru[3:0]), .in8(4'b0111), .in9(4'b0111), .in10(4'b0111),
    .in11(4'b0111), .in12(instru[3:0]), .in13(instru[3:0]), .in14(instru[3:0]), .in15(instru[3:0]),
    .out(multiplexer_1_out), .sel(slctOp));
  assign or_1_out = {24{1'b0}} | instru;  // OR_Gate or_1, 24 bits wide
  assign not_1_out = ~or_1_out;  // NOT_Gate not_1, 24 bits wide
  and and_1 (and_1_out, not_1_out[12], not_1_out[23], not_1_out[22], not_1_out[21], not_1_out[20], not_1_out[19], not_1_out[18], not_1_out[17], not_1_out[16], not_1_out[15], not_1_out[14], not_1_out[13], not_1_out[11], not_1_out[10], not_1_out[9], not_1_out[8], not_1_out[7], not_1_out[6], not_1_out[5], not_1_out[4], not_1_out[3], not_1_out[2], not_1_out[1], not_1_out[0]);
  or or_2 (or_2_out, stor, and_1_out, or_3_out);
  Multiplexer #(.width(4)) multiplexer_2 (.in0(multiplexer_1_out), .in1(4'b1111), .out(slctRegWrite), .sel(or_2_out));
  not not_2 (not_2_out, zero);
  and and_2 (and_2_out, zero, type_op_decode_1_jeq);
  or or_3 (or_3_out, type_op_decode_1_jeq, type_op_decode_1_jne, type_op_decode_1_jump);
  and and_3 (and_3_out, not_2_out, type_op_decode_1_jne);
  or or_4 (jump, and_3_out, type_op_decode_1_jump, and_2_out);

  assign ADRR8 = instru[11:4];
  assign slctRegA = instru[15:12];
  assign slctRegB = instru[11:8];
endmodule

module type_op_decode (
  input  [3:0] type_op,
  input  [3:0] op,
  output [3:0] slcOp,
  output [1:0] slctREG_in,
  output jump,
  output stor,
  output jne,
  output jeq
);

  wire and_1_out, and_2_out, and_3_out, and_4_out, and_5_out, and_6_out, and_7_out, and_8_out, and_9_out,
       and_10_out, and_11_out, and_12_out, and_13_out, and_14_out, and_15_out, and_16_out, and_17_out,
       and_18_out, not_1_out, not_2_out, not_3_out, not_4_out, not_5_out, not_6_out, not_7_out, not_8_out;

  not not_1 (not_1_out, type_op[3]);
  not not_2 (not_2_out, type_op[2]);
  not not_3 (not_3_out, type_op[1]);
  not not_4 (not_4_out, type_op[0]);
  not not_5 (not_5_out, op[3]);
  not not_6 (not_6_out, op[2]);
  not not_7 (not_7_out, op[1]);
  not not_8 (not_8_out, op[0]);
  and and_1 (and_1_out, not_1_out, not_2_out, not_3_out, not_4_out, not_5_out, not_6_out, op[0]);
  and and_2 (and_2_out, not_1_out, not_2_out, not_3_out, not_4_out, not_7_out, op[0]);
  and and_3 (and_3_out, not_1_out, not_2_out, not_3_out, not_4_out, not_5_out, op[2], op[1], not_8_out);
  and and_4 (and_4_out, not_1_out, not_2_out, not_3_out, not_4_out, op[3], not_6_out, op[1], not_8_out);
  and and_5 (and_5_out, not_1_out, not_2_out, not_3_out, not_4_out, op[3], op[2], not_7_out);
  and and_6 (and_6_out, not_1_out, not_2_out, not_3_out, type_op[0], not_5_out, not_6_out, not_7_out);
  and and_7 (and_7_out, not_1_out, not_2_out, not_3_out, type_op[0], not_5_out, not_6_out, not_8_out);
  and and_8 (and_8_out, not_1_out, not_2_out, not_3_out, not_4_out, op[3], not_7_out, op[0]);
  and and_9 (and_9_out, not_1_out, not_2_out, not_3_out, not_4_out, op[3], not_6_out, op[1], not_8_out);
  and and_10 (and_10_out, not_1_out, not_2_out, not_3_out, not_4_out, op[3], op[2], not_7_out);
  and and_11 (and_11_out, not_1_out, not_2_out, not_3_out, not_4_out, not_5_out, not_7_out, op[0]);
  and and_12 (and_12_out, not_1_out, not_2_out, not_3_out, type_op[0], not_5_out, not_6_out, op[1], not_8_out);
  and and_13 (and_13_out, not_1_out, not_2_out, not_3_out, not_4_out, op[3], op[2], not_7_out);
  and and_14 (and_14_out, not_1_out, not_2_out, not_3_out, type_op[0], not_6_out, not_7_out, op[0]);
  and and_15 (and_15_out, not_1_out, not_2_out, not_3_out, not_4_out, not_5_out, op[2], not_7_out, op[0]);
  and and_16 (and_16_out, not_1_out, not_2_out, not_3_out, not_4_out, not_5_out, op[2], op[1], not_8_out);
  and and_17 (and_17_out, not_1_out, not_2_out, not_3_out, not_4_out, op[3], not_6_out, op[1], not_8_out);
  and and_18 (and_18_out, not_1_out, not_2_out, not_3_out, not_4_out, op[3], op[2], not_7_out, not_8_out);
  and and_19 (slctREG_in[1], not_1_out, not_2_out, type_op[1], not_4_out, not_5_out, op[2], not_7_out, not_8_out);
  and and_20 (slctREG_in[0], not_1_out, not_2_out, type_op[1], not_4_out, not_5_out, not_6_out, not_7_out, op[0]);
  and and_21 (jump, not_1_out, not_2_out, type_op[1], not_4_out, not_5_out, op[2], not_7_out, op[0]);
  and and_22 (stor, not_1_out, not_2_out, type_op[1], not_4_out, not_5_out, not_6_out, op[1], not_8_out);
  and and_23 (jne, not_1_out, not_2_out, type_op[1], not_4_out, not_5_out, op[2], op[1], not_8_out);
  and and_24 (jeq, not_1_out, not_2_out, not_4_out, not_5_out, op[2], op[1], op[0]);
  or or_1 (slcOp[3], and_1_out, and_2_out, and_3_out, and_4_out, and_5_out);
  or or_2 (slcOp[2], and_6_out, and_7_out, and_8_out, and_9_out, and_10_out);
  or or_3 (slcOp[1], and_11_out, and_12_out, and_13_out);
  or or_4 (slcOp[0], and_14_out, and_15_out, and_16_out, and_17_out, and_18_out);
endmodule
