// Logisim project registry_file.circ as structural Verilog: 3 circuits, main circuit bits_registry
module bits_registry (
  input  [7:0] A,
  input  We,
  output [7:0] S
);

  wire and_1_out, clock_1_out;

  Clock clock_1 (.out(clock_1_out));
  and and_1 (and_1_out, clock_1_out, We);
  D_Flip_Flop d_ff_1 (.D(A[0]), .clk(and_1_out), .Q(S[0]));  // open: Qn, preset, reset
  D_Flip_Flop d_ff_2 (.D(A[1]), .clk(and_1_out), .Q(S[1]));  // open: Qn, preset, reset
  D_Flip_Flop d_ff_3 (.D(A[2]), .clk(and_1_out), .Q(S[2]));  // open: Qn, preset, reset
  D_Flip_Flop d_ff_4 (.D(A[3]), .clk(and_1_out), .Q(S[3]));  // open: Qn, preset, reset
  D_Flip_Flop d_ff_5 (.D(A[4]), .clk(and_1_out), .Q(S[4]));  // open: Qn, preset, reset
  D_Flip_Flop d_ff_6 (.D(A[5]), .clk(and_1_out), .Q(S[5]));  // open: Qn, preset, reset
  D_Flip_Flop d_ff_7 (.D(A[6]), .clk(and_1_out), .Q(S[6]));  // open: Qn, preset, reset
  D_Flip_Flop d_ff_8 (.D(A[7]), .clk(and_1_out), .Q(S[7]));  // open: Qn, preset, reset
endmodule

module bit_registry (
  input  A,
  input  We,
  output S
);

  wire and_1_out, clock_1_out;

  Clock clock_1 (.out(clock_1_out));
  and and_1 (and_1_out, clock_1_out, We);
  D_Flip_Flop d_ff_1 (.D(A), .clk(and_1_out), .Q(S));  // open: Qn, preset, reset
endmodule

module registry_file (
  input  [2:0] slct_c,
  input  [7:0] C,
  input  [2:0] slct_A,
  input  [2:0] slct_B,
  output [7:0] S_A,
  output [7:0] S_B,
  output S_1_bit
);

  wire decoder_1_out0, decoder_1_out1, decoder_1_out2, decoder_1_out3, decoder_1_out4, decoder_1_out5,
       decoder_1_out6, decoder_1_out7;
  wire [7:0] bit_extender_1_out, bits_registry_1_s, bits_registry_2_s, bits_registry_3_s, bits_registry_4_s,
       bits_registry_5_s, bits_registry_6_s, bits_registry_7_s;

  Decoder #(.select(3)) decoder_1 (
    .out0(decoder_1_out0), .out1(decoder_1_out1), .out2(decoder_1_out2), .out3(decoder_1_out3),
    .out4(decoder_1_out4), .out5(decoder_1_out5), .out6(decoder_1_out6), .out7(decoder_1_out7), .sel(slct_c),
    .en(1'b1));
  bits_registry bits_registry_1 (.A(C), .We(decoder_1_out0), .S(bits_registry_1_s));
  bits_registry bits_registry_2 (.A(C), .We(decoder_1_out1), .S(bits_registry_2_s));
  bits_registry bits_registry_3 (.A(C), .We(decoder_1_out2), .S(bits_registry_3_s));
  bits_registry bits_registry_4 (.A(C), .We(decoder_1_out3), .S(bits_registry_4_s));
  bits_registry bits_registry_5 (.A(C), .We(decoder_1_out4), .S(bits_registry_5_s));
  bits_registry bits_registry_6 (.A(C), .We(decoder_1_out5), .S(bits_registry_6_s));
  bits_registry bits_registry_7 (.A(C), .We(decoder_1_out6), .S(bits_registry_7_s));
  bit_registry bit_registry_1 (.A(C[0]), .We(decoder_1_out7), .S(S_1_bit));
  assign bit_extender_1_out = {{7{1'b0}}, S_1_bit};  // Bit_Extender bit_extender_1
  Multiplexer #(.select(3), .width(8)) multiplexer_1 (
    .in0(bits_registry_1_s), .in1(bits_registry_2_s), .in2(bits_registry_3_s), .in3(bits_registry_4_s),
    .in4(bits_registry_5_s), .in5(bits_registry_6_s), .in6(bits_registry_7_s), .in7(bit_extender_1_out),
    .out(S_A), .sel(slct_A));
  Multiplexer #(.select(3), .width(8)) multiplexer_2 (
    .in0(bits_registry_1_s), .in1(bits_registry_2_s), .in2(bits_registry_3_s), .in3(bits_registry_4_s),
    .in4(bits_registry_5_s), .in5(bits_registry_6_s), .in6(bits_registry_7_s), .in7(bit_extender_1_out),
    .out(S_B), .sel(slct_B));
endmodule
